# Fritzing sketch ESP8266-RS485_DIP-230-V2 (saved by Fritzing 0.9.6b)
circuit board: 5cm x 5.4cm

parts:
  J7 = female pin header, 3 pins [form="♀ (female)" part_number=AMS1117]
  J11 = double row rounded female pin header, 8 pins [form="♀ (female rounded)"]
  R1 = Resistor [tolerance=±5% resistance=1k power=0.25 package=THT]
  R2 = Resistor [tolerance=±5% resistance=1k power=0.25 package=THT]
  R3 = Resistor [tolerance=±5% resistance=1k power=0.25 package=THT]
  J12 = screw terminal, 4 pins
  R4 = Resistor [tolerance=±5% resistance=20k power=0.25 package=THT]
  R5 = Resistor [tolerance=±5% resistance=20k power=0.25 package=THT]
  R6 = Resistor [tolerance=±5% resistance=120 power=0.25 package=THT]
  MAX485 = MAX485 [package=dil08]
  R7 = Resistor [tolerance=±5% resistance=1k power=0.25 package=THT]
  R9 = Resistor [tolerance=±5% resistance=10k power=0.25 package=THT]
  R10 = Resistor [tolerance=±5% resistance=10k power=0.25 package=THT]
  Q1 = PNP-Transistor [part_number=2N2907 package="TO92 [THT]"]
  J1 = female pin header, 3 pins [form="♀ (female)"]
  R8 = Resistor [tolerance=±5% resistance=220 power=0.25 package=THT]
  J3 = female pin header, 2 pins [form="♀ (female)"]
  HLK-PM2 = HLK-PM01
  J13 = Screw terminal - 2 pins [package=THT]
  F2 = Resettable Fuse PTC [package=ptc]
  X1 = USB Connectors [package=usb-a-h]
  J2 = female pin header, 3 pins [form="♀ (female)"]

nets:
  GND: J7.pin1, J11.pin4, R3.Pin_0, J12.pin1, R5.Pin_1, MAX485.GND, R10.Pin_0, J3.pin2, HLK-PM2.-Vo, X1.GND, J2.pin1
  N1: J7.pin2, J11.pin8, R9.Pin_0, Q1.E, J2.pin3
  N2: J7.pin3, J12.pin4, R4.Pin_1, MAX485.VCC, HLK-PM2.+Vo, X1.VBUS
  N3: J11.pin1, R1.Pin_0, R2.Pin_0
  N4: J11.pin2, R7.Pin_1, R9.Pin_1
  N5: J11.pin3, R8.Pin_0
  N6: J11.pin5, MAX485.DI
  N7: J11.pin6, J2.pin2
  N8: R1.Pin_1, MAX485.RO
  N9: R2.Pin_1, R3.Pin_1
  N10: J12.pin2, R4.Pin_0, MAX485.A, J1.pin2
  N11: J12.pin3, R5.Pin_0, R6.Pin_0, MAX485.B
  N12: R6.Pin_1, J1.pin1
  N13: MAX485.RE, MAX485.DE, R10.Pin_1, Q1.C
  N14: R7.Pin_0, Q1.B
  N15: R8.Pin_1, J3.pin1
  N16: HLK-PM2.AC#0, F2.1
  N17: HLK-PM2.AC#1, J13.pin2
  N18: J13.pin1, F2.2

notes:
  GND OUT VIN
  by GJ
  GND  D+  D-  5V
  ESP/485 Bridge
  ESP/485
  - +
  LED
  CH_EN
  .
  OJO 230V
  L   N
  off/on
  on/off
  AMS1117-3.3
