# Fritzing sketch ESP8266-RS485_DIP-230 (saved by Fritzing 0.9.6b)
circuit board: 7cm x 4.5cm

parts:
  J7 = female pin header, 3 pins [form="♀ (female)" part_number=AMS1117-3.3]
  HLK-PM1 = HLK-PM01
  J8 = Screw terminal - 2 pins [package=THT]
  F1 = Resettable Fuse PTC [package=ptc]
  J11 = double row rounded female pin header, 8 pins [form="♀ (female rounded)"]
  R1 = Resistor [tolerance=±5% resistance=1k power=0.25 package=THT]
  R2 = Resistor [tolerance=±5% resistance=1k power=0.25 package=THT]
  R3 = Resistor [tolerance=±5% resistance=1k power=0.25 package=THT]
  J12 = screw terminal, 4 pins
  R4 = Resistor [tolerance=±5% resistance=20k power=0.25 package=THT]
  R5 = Resistor [tolerance=±5% resistance=20k power=0.25 package=THT]
  R6 = Resistor [tolerance=±5% resistance=120 power=0.25 package=THT]
  MAX485 = MAX485 [package=dil08]
  R7 = Resistor [tolerance=±5% resistance=1k power=0.25 package=THT]
  R9 = Resistor [tolerance=±5% resistance=10k power=0.25 package=THT]
  R10 = Resistor [tolerance=±5% resistance=10k power=0.25 package=THT]
  Q1 = PNP-Transistor [part_number=2N2907 package="TO92 [THT]"]
  J13 = female pin header, 3 pins [form="♀ (female)"]

nets:
  N1: J7.pin1, HLK-PM1.-Vo, J11.pin4, R3.Pin_0, J12.pin1, R5.Pin_1, MAX485.GND, R10.Pin_0
  N2: J7.pin2, J11.pin6, J11.pin8, R9.Pin_0, Q1.E
  N3: J7.pin3, HLK-PM1.+Vo, J12.pin4, R4.Pin_1, MAX485.VCC
  N4: HLK-PM1.AC#0, J8.pin2
  N5: HLK-PM1.AC#1, F1.1
  N6: J8.pin1, F1.2
  N7: J11.pin1, R1.Pin_1, R2.Pin_1
  N8: J11.pin2, R7.Pin_1, R9.Pin_1
  N9: J11.pin5, MAX485.DI
  N10: R1.Pin_0, MAX485.RO
  N11: R2.Pin_0, R3.Pin_1
  N12: J12.pin2, R4.Pin_0, MAX485.A, J13.pin2
  N13: J12.pin3, R5.Pin_0, R6.Pin_0, MAX485.B
  N14: R6.Pin_1, J13.pin1
  N15: MAX485.RE, MAX485.DE, R10.Pin_1, Q1.C
  N16: R7.Pin_0, Q1.B

notes:
  GND OUT VIN
  OJO 230V
  ESP/485 Bridge
  by GJ
  ESP-01
  L   N
  GND  D+  D-  5V
  AMS1117-3.3
